// Logisim project workdesign.circ as structural Verilog
module basic (
  input  Reset
);

  wire clock_1_out;
  wire [3:0] joystick_1_x;

  Joystick joystick_1 (.x(joystick_1_x));  // open: y
  Clock clock_1 (.out(clock_1_out));
  Register #(.width(4)) car_x (.D(joystick_1_x), .clr(Reset));  // open: en, clk, Q
  Counter #(.max('h60)) counter_1 (.clk(clock_1_out));  // open: load, D, count, Q, carry, up, clr
endmodule
